# Fritzing sketch ZX Spectrum PIO Board 1.1 (saved by Fritzing 0.9.9b)
stripboards: 1

parts:
  R1 = Resistor [tolerance=±5% power=0.25 resistance=10k package=THT]
  C1 = Ceramic Capacitor [capacitance=100nF voltage=35V package="100 mil [THT, multilayer]"]
  J1 = Generic shrouded header - 56 pins [form="♂ (shrouded male)" package=THT]
  IC1 = DIP - 40 pins [chip_label="Z80 PIO" package="DIP (Dual Inline) [THT]"]
  J2 = shrouded pin header, 16 pins [form="♂ (shrouded male)"]
  IC2 = DIP - 16 pins [chip_label=HEF4050B package="DIP (Dual Inline) [THT]"]
  IC3 = DIP - 16 pins [chip_label=HEF4050B package="DIP (Dual Inline) [THT]"]
  R4 = Resistor [tolerance=±5% power=0.25 resistance=220 package=THT]
  LED3 = LED - 3mm [color="Red (633nm)" current=0.030 package="3 mm [THT]"]
  LED4 = LED - 3mm [color="Red (633nm)" current=0.030 package="3 mm [THT]"]
  R5 = Resistor [tolerance=±5% power=0.25 resistance=220 package=THT]
  LED5 = LED - 3mm [color="Red (633nm)" current=0.030 package="3 mm [THT]"]
  R6 = Resistor [tolerance=±5% power=0.25 resistance=220 package=THT]
  LED6 = LED - 3mm [color="Red (633nm)" current=0.030 package="3 mm [THT]"]
  R7 = Resistor [tolerance=±5% power=0.25 resistance=220 package=THT]
  LED7 = LED - 3mm [color="Red (633nm)" current=0.030 package="3 mm [THT]"]
  R8 = Resistor [tolerance=±5% power=0.25 resistance=220 package=THT]
  LED8 = LED - 3mm [color="Red (633nm)" current=0.030 package="3 mm [THT]"]
  R9 = Resistor [tolerance=±5% power=0.25 resistance=220 package=THT]
  LED9 = LED - 3mm [color="Red (633nm)" current=0.030 package="3 mm [THT]"]
  R10 = Resistor [tolerance=±5% power=0.25 resistance=220 package=THT]
  LED10 = LED - 3mm [color="Red (633nm)" current=0.030 package="3 mm [THT]"]
  R11 = Resistor [tolerance=±5% power=0.25 resistance=220 package=THT]
  LED11 = LED - 3mm [color="Green (560nm)" current=0.030 package="3 mm [THT]"]
  R12 = Resistor [tolerance=±5% power=0.25 resistance=220 package=THT]
  LED12 = LED - 3mm [color="Green (560nm)" current=0.030 package="3 mm [THT]"]
  R13 = Resistor [tolerance=±5% power=0.25 resistance=220 package=THT]

nets:
  N1: R1.Pin_0, IC1.pin24
  5V: R1.Pin_1, C1.0, J1.pin3, IC1.pin26, IC2.pin1, IC3.pin1
  GND: C1.1, J1.pin6, IC1.pin11, J2.pin2, IC2.pin8, IC3.pin8, LED3.cathode, LED4.cathode, LED5.cathode, LED6.cathode, LED7.cathode, LED8.cathode, LED9.cathode, LED10.cathode, LED11.cathode, LED12.cathode
  CLK: J1.pin8, IC1.pin25
  A7: J1.pin21, IC1.pin4
  A6: J1.pin22, IC1.pin5
  A5: J1.pin23, IC1.pin6
  M1: J1.pin33, IC1.pin37
  RD: J1.pin39, IC1.pin35
  IORQ: J1.pin40, IC1.pin36
  INT: J1.pin44, IC1.pin23
  D4: J1.pin45, IC1.pin39
  D3: J1.pin46, IC1.pin40
  D5: J1.pin47, IC1.pin38
  D6: J1.pin48, IC1.pin3
  D2: J1.pin49, IC1.pin1
  D1: J1.pin50, IC1.pin20
  D0: J1.pin51, IC1.pin19
  D7: J1.pin54, IC1.pin2
  PA1: IC1.pin14, J2.pin6, IC3.pin9
  PA0: IC1.pin15, J2.pin3, IC3.pin11
  PB0: IC1.pin27, J2.pin16, IC3.pin5
  PB1: IC1.pin28, J2.pin15, IC3.pin3
  PB2: IC1.pin29, J2.pin14, IC2.pin14
  PB3: IC1.pin30, J2.pin13, IC2.pin11
  PB4: IC1.pin31, J2.pin12, IC2.pin9
  PB5: IC1.pin32, J2.pin11, IC2.pin7
  PB6: IC1.pin33, J2.pin10, IC2.pin5
  PB7: IC1.pin34, J2.pin9, IC2.pin3
  N2: IC2.pin2, R4.Pin_1
  N3: IC2.pin4, R5.Pin_1
  N4: IC2.pin6, R6.Pin_1
  N5: IC2.pin10, R7.Pin_1
  N6: IC2.pin12, R8.Pin_1
  N7: IC2.pin15, R9.Pin_1
  N8: IC3.pin2, R10.Pin_1
  N9: IC3.pin4, R11.Pin_1
  N10: IC3.pin10, R12.Pin_1
  N11: IC3.pin12, R13.Pin_1
  N12: R4.Pin_0, LED3.anode
  N13: LED4.anode, R5.Pin_0
  N14: LED5.anode, R6.Pin_0
  N15: LED6.anode, R7.Pin_0
  N16: LED7.anode, R8.Pin_0
  N17: LED8.anode, R9.Pin_0
  N18: LED9.anode, R10.Pin_0
  N19: LED10.anode, R11.Pin_0
  N20: LED11.anode, R12.Pin_0
  N21: LED12.anode, R13.Pin_0

custom parts:
  Generic shrouded header - 56 pins: Generic shrouded header
  DIP - 40 pins: A DIP stand-in part for whatever IC you want. With 40 pins on a 600mil dual inline package (DIP) footprint.
  DIP - 16 pins: A DIP stand-in part for whatever IC you want. With 16 pins on a 300mil dual inline package (DIP) footprint.
